# Fritzing sketch 2.2 TFT (saved by Fritzing 0.9.3b)
breadboards: 1

parts:
  Part1 = adafruit [part_number=1480]
  Raspberry_Pi_1 = Raspberry Pi 3 [part_number=RPI-3-V1.2]

nets:
  N1: Part1.connector5, Raspberry_Pi_1.GND
  N2: Part1.connector6, Raspberry_Pi_1.3v3
  N3: Part1.connector7, Raspberry_Pi_1.GIPO24
  N4: Part1.connector8, Raspberry_Pi_1.GIPO25
  N5: Part1.connector10, Raspberry_Pi_1.GIPO8
  N6: Part1.connector11, Raspberry_Pi_1.GIPO10
  N7: Part1.connector13, Raspberry_Pi_1.GIPO11
